# Fritzing sketch beacon_mega (saved by Fritzing 0.4.3b)
breadboards: 2

parts:
  Arduino_Ethernet_Shield1 = Arduino Ethernet Shield
  IC1 = IC, DIP package, 28 pins [chip_label=TLC5940 spacing=300mil]
  R1 = Resistor [resistance=2k package=THT]
  J4 = female pin header, 4 pins [form="♂ (male)"]
  J4_2 = female pin header, 4 pins [form="♂ (male)"]
  J4_3 = female pin header, 4 pins [form="♂ (male)"]
  J4_4 = female pin header, 4 pins [form="♂ (male)"]

nets:
  N1: Arduino_Ethernet_Shield1.GND, R1.Pin_0
  N2: Arduino_Ethernet_Shield1.D7, IC1.pin26
  N3: Arduino_Ethernet_Shield1.D2, IC1.pin25
  N4: Arduino_Ethernet_Shield1.VIN, J4.pin1, J4_2.pin1, J4_3.pin1, J4_4.pin1
  N5: IC1.pin9, J4_3.pin4
  N6: IC1.pin11, J4_3.pin3
  N7: IC1.pin19, IC1.pin21

notes:
  Arduino Mega with a v5 Ethernet Shield.
