# Fritzing sketch beacon_uno (saved by Fritzing 0.4.3b)
breadboards: 2

parts:
  Arduino_Ethernet_Shield1 = Arduino Ethernet Shield
  IC1 = IC, DIP package, 28 pins [chip_label=TLC5940 spacing=300mil]
  R1 = Resistor [resistance=2k package=THT]
  J4 = female pin header, 4 pins [form="♂ (male)"]
  J4_2 = female pin header, 4 pins [form="♂ (male)"]
  J4_3 = female pin header, 4 pins [form="♂ (male)"]
  J4_4 = female pin header, 4 pins [form="♂ (male)"]
  Arduino1 = Arduino

nets:
  N1: Arduino_Ethernet_Shield1.GND, IC1.pin22, IC1.pin27, R1.Pin_0
  N2: Arduino_Ethernet_Shield1.SS, Arduino_Ethernet_Shield1.D8
  N3: Arduino_Ethernet_Shield1.D9, IC1.pin24
  N4: Arduino_Ethernet_Shield1.D7, IC1.pin26
  N5: Arduino_Ethernet_Shield1.D3, IC1.pin18
  N6: Arduino_Ethernet_Shield1.D2, IC1.pin25
  N7: Arduino_Ethernet_Shield1.+5V, IC1.pin19, IC1.pin21
  N8: Arduino_Ethernet_Shield1.VIN, J4.pin1, J4_2.pin1, J4_3.pin1, J4_4.pin1
  N9: IC1.pin1, J4_4.pin2
  N10: IC1.pin2, J4_4.pin3
  N11: IC1.pin3, J4.pin4
  N12: IC1.pin4, J4.pin2
  N13: IC1.pin5, J4.pin3
  N14: IC1.pin6, J4_2.pin4
  N15: IC1.pin7, J4_2.pin2
  N16: IC1.pin8, J4_2.pin3
  N17: IC1.pin9, J4_3.pin4
  N18: IC1.pin10, J4_3.pin2
  N19: IC1.pin11, J4_3.pin3
  N20: IC1.pin20, R1.Pin_1
  N21: IC1.pin23, Arduino1.D10
  N22: IC1.pin28, J4_4.pin4

notes:
  To use an Arduino Uno with an Ethernet Shield, the shield must be plugged with pin 10 sticking out.
